# Fritzing sketch projekt (saved by Fritzing 0.9.3b)
breadboards: 1

parts:
  Part1 = RFID-RC522-v2
  M7 = Dagu DGServo 9g (Top view) [part_number=RS001B]
  PWM1 = PCA9685 16x12-bit PWM Breakout
  J1 = Dagu DGServo 9g header connector (female) [package=THT]
  M8 = Dagu DGServo 9g (Top view) [part_number=RS001B]
  J2 = Dagu DGServo 9g header connector (female) [package=THT]
  M9 = Dagu DGServo 9g (Top view) [part_number=RS001B]
  J3 = Dagu DGServo 9g header connector (female) [package=THT]
  M10 = Dagu DGServo 9g (Top view) [part_number=RS001B]
  J4 = Dagu DGServo 9g header connector (female) [package=THT]
  M11 = Dagu DGServo 9g (Top view) [part_number=RS001B]
  J5 = Dagu DGServo 9g header connector (female) [package=THT]
  J6 = Dagu DGServo 9g header (male) [package=THT]
  MCU1 = Raspberry Pi Zero
  Matrix_keypad1 = KEYPAD 4x4
  LCD2004-I2C1 = LCD2004-I2C

nets:
  N1: Part1.SDA, MCU1.pin_24
  N2: Part1.SCK, MCU1.pin_23
  N3: Part1.MOSI, MCU1.pin_19
  N4: Part1.MISO, MCU1.pin_21
  GND: Part1.GND, PWM1.no_name_yet#501, PWM1.no_name_yet#1000, PWM1.no_name_yet#1001, PWM1.no_name_yet#1002, PWM1.no_name_yet#1003, PWM1.no_name_yet#1004, MCU1.pin_6, MCU1.pin_7, MCU1.pin_9, MCU1.pin_25, LCD2004-I2C1.GND
  N5: Part1.RST, MCU1.pin_22
  N6: Part1.3.3V, PWM1.no_name_yet#505, MCU1.pin_1, MCU1.pin_17
  GND_2: M7.gnd, J1.gnd, J6.gnd
  VCC: M7.vcc, J1.Vcc, J6.Vcc
  N7: M7.pulse, PWM1.no_name_yet#0, J1.pulse, J6.pulse
  N8: PWM1.no_name_yet#1, M8.pulse, J2.pulse
  N9: PWM1.no_name_yet#2, M9.pulse, J3.pulse
  N10: PWM1.no_name_yet#3, M10.pulse, J4.pulse
  N11: PWM1.no_name_yet#4, M11.pulse, J5.pulse
  N12: PWM1.no_name_yet#100, PWM1.no_name_yet#101, PWM1.no_name_yet#102, PWM1.no_name_yet#103, PWM1.no_name_yet#104, PWM1.no_name_yet#506, MCU1.pin_2, MCU1.pin_4, LCD2004-I2C1.VCC
  N13: PWM1.no_name_yet#503, MCU1.pin_5, LCD2004-I2C1.SCL
  N14: PWM1.no_name_yet#504, MCU1.pin_3, LCD2004-I2C1.SDA
  GND_3: M8.gnd, J2.gnd
  VCC_2: M8.vcc, J2.Vcc
  GND_4: M9.gnd, J3.gnd
  VCC_3: M9.vcc, J3.Vcc
  GND_5: M10.gnd, J4.gnd
  VCC_4: M10.vcc, J4.Vcc
  GND_6: M11.gnd, J5.gnd
  VCC_5: M11.vcc, J5.Vcc
  N15: MCU1.pin_31, Matrix_keypad1.col4
  N16: MCU1.pin_32, Matrix_keypad1.row4
  N17: MCU1.pin_33, Matrix_keypad1.col3
  N18: MCU1.pin_35, Matrix_keypad1.col2
  N19: MCU1.pin_36, Matrix_keypad1.row3
  N20: MCU1.pin_37, Matrix_keypad1.col1
  N21: MCU1.pin_38, Matrix_keypad1.row2
  N22: MCU1.pin_40, Matrix_keypad1.row1

custom parts:
  RFID-RC522-v2: A simple China made RFID-RC522 Reader; do check the pin labels, as this is a MFRC522 based clone.
  KEYPAD 4x4: Matrix keypad 16 buttons, 4 rows x 4 columns
  LCD2004-I2C: A standard character display with 4x20 characters. Comes in many colors with LCM2004 IIC attached.
